# Fritzing sketch DartboardInterface (saved by Fritzing 0.8.3b)
breadboards: 2

parts:
  U1 = 74HC595 [package="DIP16 [THT]"]
  U2 = 74HC595 [package="DIP16 [THT]"]
  Part1 = Arduino Micro (Rev3)
  J1 = Piezo Speaker
  R1 = Resistor [tolerance=±5% resistance=100 package=THT]
  J2 = shrouded pin header, 20 pins [form="♂ (shrouded male)"]
  R2 = Resistor [tolerance=±5% resistance=10k package=THT]
  R3 = Resistor [tolerance=±5% resistance=10k package=THT]
  R4 = Resistor [tolerance=±5% resistance=10k package=THT]
  R5 = Resistor [tolerance=±5% resistance=10k package=THT]
  R6 = Resistor [tolerance=±5% resistance=10k package=THT]
  R7 = Resistor [tolerance=±5% resistance=10k package=THT]
  R8 = Resistor [tolerance=±5% resistance=10k package=THT]
  R9 = Resistor [tolerance=±5% resistance=10k package=THT]
  U3 = 74HC589 [package="DIP16 [THT]"]
  LED1 = LED - 5mm [color="Red (633nm)" package="5 mm [THT]"]
  LED2 = LED - 5mm [color="Yellow (595nm)" package="5 mm [THT]"]
  LED3 = LED - 5mm [color="Green (555nm)" package="5 mm [THT]"]
  LED4 = LED - 5mm [color="Green (555nm)" package="5 mm [THT]"]
  LED5 = LED - 5mm [color="Red (633nm)" package="5 mm [THT]"]
  LED6 = LED - 5mm [color="Yellow (595nm)" package="5 mm [THT]"]
  R10 = Resistor [tolerance=±5% resistance=220 package=THT]
  R11 = Resistor [tolerance=±5% resistance=220 package=THT]
  R12 = Resistor [tolerance=±5% resistance=220 package=THT]
  R13 = Resistor [tolerance=±5% resistance=220 package=THT]
  R14 = Resistor [tolerance=±5% resistance=220 package=THT]
  R15 = Resistor [tolerance=±5% resistance=220 package=THT]

nets:
  N1: U1.Q1, R15.Pin_0
  N2: U1.Q2, R14.Pin_0
  N3: U1.Q3, R10.Pin_0
  N4: U1.Q4, R11.Pin_0
  N5: U1.Q5, R12.Pin_0
  N6: U1.Q6, J2.pin10
  N7: U1.Q7, J2.pin9
  GND: U1.GND, U1.OE, U2.GND, U2.OE, Part1.GND, J1.pin1, R2.Pin_1, R3.Pin_1, R4.Pin_1, R5.Pin_1, R6.Pin_1, R7.Pin_1, R8.Pin_1, R9.Pin_0, U3.GND, U3.OE, LED1.cathode, LED2.cathode, LED3.cathode, LED4.cathode, LED5.cathode, LED6.cathode
  VCC: U1.MR, U1.VCC, U2.MR, U2.VCC, Part1.5V, U3.VCC
  N8: U1.SH_CP, U2.SH_CP, Part1.D5_PWM
  N9: U1.ST_CP, U2.ST_CP, Part1.D4_PWM/A6
  N10: U1.DS, U2.Q7'
  N11: U1.Q0, R13.Pin_0
  N12: U2.Q1, J2.pin7
  N13: U2.Q2, J2.pin6
  N14: U2.Q3, J2.pin5
  N15: U2.Q4, J2.pin4
  N16: U2.Q5, J2.pin3
  N17: U2.Q6, J2.pin2
  N18: U2.Q7, J2.pin1
  N19: U2.DS, Part1.D6_PWM/A7
  N20: U2.Q0, J2.pin8
  N21: Part1.D7, U3.QH
  N22: Part1.D8_PWM/A8, U3.SHIFT_CLOCK
  N23: Part1.D9_PWM/A9, U3.LATCH_CLOCK
  N24: Part1.D10_PWM/A10, U3.SERIAL_SHIFT/PARALLEL_LOAD
  N25: Part1.D12_PWM/A11, R1.Pin_0
  N26: J1.pin2, R1.Pin_1
  N27: J2.pin14, R8.Pin_0, U3.B
  N28: J2.pin15, R6.Pin_0, U3.C
  N29: J2.pin16, R5.Pin_0, U3.D
  N30: J2.pin17, R4.Pin_0, U3.E
  N31: J2.pin18, R7.Pin_0, U3.F
  N32: J2.pin19, R3.Pin_0, U3.G
  N33: J2.pin20, R2.Pin_0, U3.H
  N34: R9.Pin_1, U3.A
  N35: LED1.anode, R10.Pin_1
  N36: LED2.anode, R11.Pin_1
  N37: LED3.anode, R12.Pin_1
  N38: LED4.anode, R14.Pin_1
  N39: LED5.anode, R13.Pin_1
  N40: LED6.anode, R15.Pin_1

custom parts:
  74HC589: 8-bit parallel-inputs/serial-output shift register
